# Fritzing sketch pico-servo (saved by Fritzing 0.9.3b)
breadboards: 1

parts:
  Mod1 = Raspberry Pi Pico (Kawoom)
  J1 = Basic Servo

nets:
  N1: Mod1.pin_3, Mod1.pin_42, J1.gnd
  N2: Mod1.pin_20, J1.pulse
  N3: Mod1.pin_40, J1.vcc

custom parts:
  Raspberry Pi Pico (Kawoom): Raspberry Pi Pico. Based around the RP2040 microcontroller the Pico is a low cost microcontroller device bringing Raspberry Pi quality, cost, and easy of use to the microcontroller space. Jan 2021, Split part in to two versions: SMD (this one) and tht. This one is single sided and uses the castellation pads to solder the module to the board (no holes, other than for the USB connector!). The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
